// Logisim project counter.circ as structural Verilog: 4 circuits, main circuit main
module main (
  input  in_1,
  output Q0,
  output Q1,
  output Q2,
  output Q3,
  output Q4
);

  wire d_6_q;

  D d_1 (.C(in_1), .Q(Q0));  // open: RES
  D d_2 (.C(Q0), .RES(d_6_q), .Q(Q1));
  D d_3 (.C(Q1), .Q(Q2));  // open: RES
  D d_4 (.C(Q2), .RES(d_6_q), .Q(Q3));
  D d_5 (.C(Q3), .Q(Q4));  // open: RES
  D d_6 (.C(Q4), .RES(d_6_q), .Q(d_6_q));
endmodule

module RS (
  input  S,
  input  C,
  input  R,
  input  RES,
  output nQ,
  output Q
);

  wire and_1_out, and_2_out, not_1_out, not_2_out, not_3_out, or_1_out, or_2_out, or_3_out, por_1_out;

  POR por_1 (.out(por_1_out));
  and and_1 (and_1_out, S, C);
  and and_2 (and_2_out, C, R);
  not not_1 (not_1_out, or_2_out);
  not not_2 (not_2_out, RES);
  or or_1 (or_1_out, RES, not_1_out);
  or or_2 (or_2_out, and_1_out, Q);
  or or_3 (or_3_out, nQ, and_2_out);
  not not_3 (not_3_out, or_3_out);
  and and_3 (Q, not_3_out, not_2_out);
  or or_4 (nQ, por_1_out, or_1_out);
endmodule

module T (
  input  D,
  input  C,
  input  RES,
  output nQ,
  output Q
);

  wire not_1_out;

  not not_1 (not_1_out, D);
  RS rs_1 (.S(D), .C(C), .R(not_1_out), .RES(RES), .nQ(nQ), .Q(Q));
endmodule

module D (
  input  C,
  input  RES,
  output Q
);

  wire not_1_out, t_1_q, t_2_nq;

  not not_1 (not_1_out, C);
  T t_1 (.D(t_2_nq), .C(not_1_out), .RES(RES), .Q(t_1_q));  // open: nQ
  T t_2 (.D(t_1_q), .C(C), .RES(RES), .nQ(t_2_nq), .Q(Q));
endmodule
