// Logisim project lfsr.circ as structural Verilog: 4 circuits, main circuit main
module main (
  input  set0,
  input  set1,
  input  set2,
  input  set3,
  input  set4,
  input  set5,
  input  set6,
  input  set7,
  input  SetConfig,
  input  Click,
  input  Reset,
  output q0,
  output q1,
  output q2,
  output q3,
  output q4,
  output q5,
  output q6,
  output q7
);

  wire setter_1_q0, setter_1_q1, setter_1_q2, setter_1_q3, setter_1_q4, setter_1_q5, setter_1_q6,
       setter_1_q7, xor_1_out, xor_2_out, xor_3_out, xor_4_out;

  Setter setter_1 (
    .s0(set0), .s1(set1), .s2(set2), .s3(set3), .s4(set4), .s5(set5), .s6(set6), .s7(set7), .Set(SetConfig),
    .q0(setter_1_q0), .q1(setter_1_q1), .q2(setter_1_q2), .q3(setter_1_q3), .q4(setter_1_q4),
    .q5(setter_1_q5), .q6(setter_1_q6), .q7(setter_1_q7));
  xor xor_1 (xor_1_out, q0, q4);
  xor xor_2 (xor_2_out, q0, q5);
  xor xor_3 (xor_3_out, q0, q6);
  xor xor_4 (xor_4_out, q0, q7);
  DDtrig ddtrig_1 (.SetQ(setter_1_q0), .D(q1), .C(Click), .SetNQ(Reset), .Q(q0));  // open: nQ
  DDtrig ddtrig_2 (.SetQ(setter_1_q1), .D(q2), .C(Click), .SetNQ(Reset), .Q(q1));  // open: nQ
  DDtrig ddtrig_3 (.SetQ(setter_1_q2), .D(q3), .C(Click), .SetNQ(Reset), .Q(q2));  // open: nQ
  DDtrig ddtrig_4 (.SetQ(setter_1_q3), .D(xor_1_out), .C(Click), .SetNQ(Reset), .Q(q3));  // open: nQ
  DDtrig ddtrig_5 (.SetQ(setter_1_q4), .D(xor_2_out), .C(Click), .SetNQ(Reset), .Q(q4));  // open: nQ
  DDtrig ddtrig_6 (.SetQ(setter_1_q5), .D(xor_3_out), .C(Click), .SetNQ(Reset), .Q(q5));  // open: nQ
  DDtrig ddtrig_7 (.SetQ(setter_1_q6), .D(xor_4_out), .C(Click), .SetNQ(Reset), .Q(q6));  // open: nQ
  DDtrig ddtrig_8 (.SetQ(setter_1_q7), .D(q0), .C(Click), .SetNQ(Reset), .Q(q7));  // open: nQ
endmodule

module Dtrig (
  input  setQ,
  input  D,
  input  C,
  input  SetNQ,
  output Q,
  output nQ
);

  wire and_1_out, and_2_out, and_3_out, and_4_out, not_1_out, not_2_out, not_3_out, not_4_out, not_5_out,
       not_7_out, por_1_out;

  not not_1 (not_1_out, setQ);
  not not_2 (not_2_out, SetNQ);
  not not_3 (not_3_out, D);
  and and_1 (and_1_out, D, C, not_2_out);
  and and_2 (and_2_out, not_1_out, not_3_out, C);
  not not_4 (not_4_out, and_1_out);
  not not_5 (not_5_out, and_2_out);
  POR por_1 (.out(por_1_out));
  and and_3 (and_3_out, not_1_out, not_4_out, nQ);
  not not_6 (Q, and_3_out);
  and and_4 (and_4_out, Q, not_5_out, not_2_out);
  not not_7 (not_7_out, and_4_out);
  or or_1 (nQ, not_7_out, por_1_out);
endmodule

module DDtrig (
  input  SetQ,
  input  D,
  input  C,
  input  SetNQ,
  output Q,
  output nQ
);

  wire dtrig_1_q, not_1_out, not_2_out;

  not not_1 (not_1_out, C);
  not not_2 (not_2_out, not_1_out);
  Dtrig dtrig_1 (.setQ(SetQ), .D(D), .C(not_1_out), .SetNQ(SetNQ), .Q(dtrig_1_q));  // open: nQ
  Dtrig dtrig_2 (.setQ(SetQ), .D(dtrig_1_q), .C(not_2_out), .SetNQ(SetNQ), .Q(Q), .nQ(nQ));
endmodule

module Setter (
  input  s0,
  input  s1,
  input  s2,
  input  s3,
  input  s4,
  input  s5,
  input  s6,
  input  s7,
  input  Set,
  output q0,
  output q1,
  output q2,
  output q3,
  output q4,
  output q5,
  output q6,
  output q7
);

  and and_1 (q0, s0, Set);
  and and_2 (q1, s1, Set);
  and and_3 (q2, s2, Set);
  and and_4 (q3, s3, Set);
  and and_5 (q4, s4, Set);
  and and_6 (q5, s5, Set);
  and and_7 (q6, s6, Set);
  and and_8 (q7, s7, Set);
endmodule
